# Fritzing sketch pcr (saved by Fritzing 0.9.2b)
breadboards: 1

parts:
  12V_10A_Power = Power plug
  Peltier = Peltier Element
  R1 = Resistor [tolerance=±5% resistance=10k package=THT]
  Q1 = Basic FET N-Channel [package="TO220 [THT]"]
  Off/On_Switch = Pushbutton [package=THT]
  R2 = Resistor [tolerance=±5% resistance=10k package=THT]
  Q2 = Basic FET N-Channel [package="TO220 [THT]"]
  Heat_Pad = Inductor [package="400 mil [THT]"]
  Part1 = Arduino Uno (Rev3)
  U1 = LCD-16X2 [package=lcd-16x2_noholes]  # not connected
  U2 = mystery part, 4 pins [chip_label=I2C spacing=300mil]
  Temp_Sensor = TMP36 [package=to-92]

nets:
  N1: 12V_10A_Power.GND, Off/On_Switch.leg1
  VCC: 12V_10A_Power.VCC, Peltier.pin2, Heat_Pad.pin_1, Part1.VIN
  N2: Peltier.pin1, Q1.drain
  GND: R1.Pin_0, Q1.source, Off/On_Switch.leg0, R2.Pin_0, Q2.source, Part1.GND, U2.pin1, Temp_Sensor.GND
  N3: R1.Pin_1, Q1.gate, Part1.D6_PWM
  N4: R2.Pin_1, Q2.gate, Part1.D5_PWM
  N5: Q2.drain, Heat_Pad.pin_0
  N6: Part1.A0, Temp_Sensor.VOUT
  N7: Part1.A4/SDA, U2.pin3
  N8: Part1.A5/SCL, U2.pin4
  5V: Part1.5V, U2.pin2, Temp_Sensor.VCC

notes:
  5V from Arduino
  12V 10A from ext. PS
  Cooler
  Heater
  Sensor
